// Logisim project tp_5.circ as structural Verilog: 1 circuit, main circuit main
module main (
  input  [2:0] in_1
);

  wire A_q, adder_1_out, B_q, demultiplexer_1_out0, demultiplexer_1_out1, multiplexer_1_out, register_1_q;
  wire [7:0] clock_1_out, PC_q, ram_1_dout, register_2_q, rom_1_data;

  RAM ram_1 (.addr(register_2_q), .oe(1'b1), .clk(clock_1_out[0]), .dout(ram_1_dout));  // open: we, din
  Clock clock_1 (.out(clock_1_out[0]));
  Counter PC (.D(clock_1_out), .Q(PC_q));  // open: clr, load, up, count, clk, carry
  ROM rom_1 (.addr(PC_q), .data(rom_1_data));
  Multiplexer multiplexer_1 (.in0(adder_1_out), .in1(ram_1_dout[0]), .out(multiplexer_1_out));  // open: sel
  Register #(.width(1)) A (.D(multiplexer_1_out), .Q(A_q));  // open: en, clk, clr
  Register #(.width(1)) B (.D(ram_1_dout[0]), .Q(B_q));  // open: en, clk, clr
  Adder #(.width(1)) adder_1 (.a(A_q), .b(B_q), .out(adder_1_out));  // open: cin, cout
  Demultiplexer demultiplexer_1 (
    .out0(demultiplexer_1_out0), .out1(demultiplexer_1_out1), .in(rom_1_data[0]));  // open: sel
  Register #(.width(1)) register_1 (.D(demultiplexer_1_out0), .Q(register_1_q));  // open: en, clk, clr
  Register #(.width(1)) register_2 (.D(demultiplexer_1_out1), .Q(register_2_q[0]));  // open: en, clk, clr
  Register #(.width(3)) FLAGS (.D(in_1));  // open: en, clk, Q, clr
  // Pins of 1 and 8 bits meet at clock_1_out
  // Pins of 1 and 8 bits meet at ram_1_dout
  // Pins of 1 and 8 bits meet at rom_1_data
  // Pins of 1 and 8 bits meet at register_2_q
endmodule
